// Logisim project 214a.circ as structural Verilog: 1 circuit, main circuit main
module main (
);

  wire and_1_out, and_2_out, and_3_out, and_4_out, not_1_out, not_2_out, not_3_out, not_4_out, not_5_out,
       not_6_out, undriven, undriven_2, undriven_3;

  not not_1 (not_1_out, undriven_2);
  and and_1 (and_1_out, undriven, undriven_2);
  not not_2 (not_2_out, undriven);
  and and_2 (and_2_out, not_2_out, not_1_out);
  and and_3 (and_3_out, not_1_out, undriven_3);
  not not_3 (not_3_out, and_1_out);
  and and_4 (and_4_out, not_3_out, not_4_out, not_5_out);
  not not_4 (not_4_out, and_2_out);
  not not_5 (not_5_out, and_3_out);
  not not_6 (not_6_out, and_4_out);

  // Notes on the sheet:
  //   x
  //   y
  //   z
  //   F = xy + x'y' + y'z
endmodule
