// Logisim project hw2-1a.circ as structural Verilog: 1 circuit, main circuit main
module main (
);

  wire and_1_out, and_2_out, and_3_out, not_1_out, not_2_out, not_3_out, undriven, undriven_2, undriven_3,
       undriven_4;

  not not_1 (not_1_out, undriven);
  and and_1 (and_1_out, not_1_out, undriven_2);
  not not_2 (not_2_out, and_1_out);
  and and_2 (and_2_out, not_2_out, undriven_3);
  not not_3 (not_3_out, and_2_out);
  and and_3 (and_3_out, not_3_out, undriven_4);

  // Notes on the sheet:
  //   a
  //   1
  //   b
  //   a.b
  //   1
  //   (a.b)'
endmodule
