// Logisim project hw2-3-1.circ as structural Verilog: 2 circuits, main circuit main
module main (
);

  wire n3_to_8_decoder_1_out_4, n3_to_8_decoder_1_out_5, n3_to_8_decoder_1_out_6, n3_to_8_decoder_1_out_8,
       or_1_out, undriven, undriven_2, undriven_3;

  _3_to_8_decoder u_3_to_8_decoder_1 (
    .in_1(undriven), .in_2(undriven_2), .in_3(undriven_3), .out_4(n3_to_8_decoder_1_out_4),
    .out_5(n3_to_8_decoder_1_out_5), .out_6(n3_to_8_decoder_1_out_6), .out_8(n3_to_8_decoder_1_out_8));  // open: out_7, out_9, out_10, out_11
  or or_1 (or_1_out, n3_to_8_decoder_1_out_4, n3_to_8_decoder_1_out_5, n3_to_8_decoder_1_out_6, n3_to_8_decoder_1_out_8);

  // Notes on the sheet:
  //   a
  //   b
  //   c
endmodule

module _3_to_8_decoder (
  input  in_1,
  input  in_2,
  input  in_3,
  output out_4,
  output out_5,
  output out_6,
  output out_7,
  output out_8,
  output out_9,
  output out_10,
  output out_11
);

  wire not_1_out, not_2_out, not_3_out;

  not not_1 (not_1_out, in_1);
  not not_2 (not_2_out, in_2);
  not not_3 (not_3_out, in_3);
  and and_1 (out_4, in_1, in_2, in_3);
  and and_2 (out_5, in_1, in_2, not_3_out);
  and and_3 (out_6, in_1, not_2_out, in_3);
  and and_4 (out_7, in_1, not_2_out, not_3_out);
  and and_5 (out_8, not_1_out, in_2, in_3);
  and and_6 (out_9, not_1_out, in_2, not_3_out);
  and and_7 (out_10, not_1_out, not_2_out, in_3);
  and and_8 (out_11, not_1_out, not_2_out, not_3_out);
endmodule
