// Logisim project hw2-3-2.circ as structural Verilog: 2 circuits, main circuit main
module main (
);

  wire n3_to_8_decoder_active_low_with_active_low_enable_1_out_5,
       n3_to_8_decoder_active_low_with_active_low_enable_1_out_6,
       n3_to_8_decoder_active_low_with_active_low_enable_1_out_7,
       n3_to_8_decoder_active_low_with_active_low_enable_1_out_9, nand_1_out, undriven, undriven_2,
       undriven_3, undriven_4;

  _3_to_8_decoder__active_low_with_active_low_enable u_3_to_8_decoder_active_low_with_active_low_enable_1 (
    .in_1(undriven), .in_2(undriven_2), .in_3(undriven_3), .in_4(undriven_4),
    .out_5(n3_to_8_decoder_active_low_with_active_low_enable_1_out_5),
    .out_6(n3_to_8_decoder_active_low_with_active_low_enable_1_out_6),
    .out_7(n3_to_8_decoder_active_low_with_active_low_enable_1_out_7),
    .out_9(n3_to_8_decoder_active_low_with_active_low_enable_1_out_9));  // open: out_8, out_10, out_11, out_12
  nand nand_1 (nand_1_out, n3_to_8_decoder_active_low_with_active_low_enable_1_out_5, n3_to_8_decoder_active_low_with_active_low_enable_1_out_6, n3_to_8_decoder_active_low_with_active_low_enable_1_out_7, n3_to_8_decoder_active_low_with_active_low_enable_1_out_9);

  // Notes on the sheet:
  //   a
  //   b
  //   c
  //   E
endmodule

module _3_to_8_decoder__active_low_with_active_low_enable (
  input  in_1,
  input  in_2,
  input  in_3,
  input  in_4,
  output out_5,
  output out_6,
  output out_7,
  output out_8,
  output out_9,
  output out_10,
  output out_11,
  output out_12
);

  wire and_1_out, and_2_out, and_3_out, and_4_out, and_5_out, and_6_out, and_7_out, and_8_out, not_1_out,
       not_2_out, not_3_out, not_4_out;

  not not_1 (not_1_out, in_1);
  not not_2 (not_2_out, in_2);
  not not_3 (not_3_out, in_3);
  not not_4 (not_4_out, in_4);
  and and_1 (and_1_out, in_1, in_2, not_4_out, in_3);
  and and_2 (and_2_out, in_1, in_2, not_3_out, not_4_out);
  and and_3 (and_3_out, in_1, not_2_out, in_3, not_4_out);
  and and_4 (and_4_out, in_1, not_2_out, not_3_out, not_4_out);
  and and_5 (and_5_out, not_1_out, in_2, in_3, not_4_out);
  and and_6 (and_6_out, not_1_out, in_2, not_3_out, not_4_out);
  and and_7 (and_7_out, not_1_out, not_2_out, in_3, not_4_out);
  and and_8 (and_8_out, not_1_out, not_2_out, not_3_out, not_4_out);
  not not_5 (out_5, and_1_out);
  not not_6 (out_6, and_2_out);
  not not_7 (out_7, and_3_out);
  not not_8 (out_8, and_4_out);
  not not_9 (out_9, and_5_out);
  not not_10 (out_10, and_6_out);
  not not_11 (out_11, and_7_out);
  not not_12 (out_12, and_8_out);
endmodule
