// Logisim project hw4-1a.circ as structural Verilog: 1 circuit, main circuit main
module main (
  input  [1:0] B_D
);

  wire multiplexer_1_out;

  Multiplexer #(.select(2)) multiplexer_1 (
    .in0(1'b1), .in1(1'b0), .in2(1'b0), .in3(1'b1), .out(multiplexer_1_out), .sel(B_D));  // open: en

  // Notes on the sheet:
  //   f(A, B, C, D)
endmodule
