// Logisim project hw4-1b.circ as structural Verilog: 1 circuit, main circuit g(A, B, C, D)
module g_A__B__C__D (
  input  B,
  input  [1:0] A_D
);

  wire multiplexer_1_out, not_1_out, not_2_out;

  not not_1 (not_1_out, B);
  Multiplexer #(.select(2)) multiplexer_1 (
    .in0(B), .in1(1'b0), .in2(1'b0), .in3(not_1_out), .out(multiplexer_1_out), .sel(A_D));  // open: en
  not not_2 (not_2_out, multiplexer_1_out);

  // Notes on the sheet:
  //   g(A, B, C, D)
endmodule
