// Logisim project hw4-3.circ as structural Verilog: 1 circuit, main circuit main
module main (
);

  wire nand_1_out, nor_1_out, undriven, undriven_2;

  nor nor_1 (nor_1_out, undriven, nand_1_out);
  nand nand_1 (nand_1_out, nor_1_out, undriven_2);

  // Notes on the sheet:
  //   1
  //   1
  //   0
  //   1
endmodule
