// Logisim project hw4-4a.circ as structural Verilog: 2 circuits, main circuit main
module main (
  input  S,
  input  R,
  output out_3,
  output out_4
);

  wire and_w_inversion_1_out_3, and_w_inversion_2_out_3;

  AND_w__Inversion and_w_inversion_1 (.in_1(out_4), .in_2(1'b1), .out_3(and_w_inversion_1_out_3));
  AND_w__Inversion and_w_inversion_2 (.in_1(out_3), .in_2(1'b1), .out_3(and_w_inversion_2_out_3));
  AND_w__Inversion and_w_inversion_3 (.in_1(S), .in_2(and_w_inversion_1_out_3), .out_3(out_3));
  AND_w__Inversion and_w_inversion_4 (.in_1(R), .in_2(and_w_inversion_2_out_3), .out_3(out_4));
endmodule

module AND_w__Inversion (
  input  in_1,
  input  in_2,
  output out_3
);

  wire not_1_out;

  not not_1 (not_1_out, in_1);
  and and_1 (out_3, not_1_out, in_2);
endmodule
