// Logisim project hw4-4b.circ as structural Verilog: 2 circuits, main circuit main
module main (
  input  S
);

  wire xor_w_inversion_1_out_3;

  XOR_w__Inversion xor_w_inversion_1 (.in_1(S), .in_2(1'b0), .out_3(xor_w_inversion_1_out_3));
endmodule

module XOR_w__Inversion (
  input  in_1,
  input  in_2,
  output out_3
);

  wire not_1_out;

  not not_1 (not_1_out, in_1);
  xor xor_1 (out_3, not_1_out, in_2);
endmodule
