// Logisim project hw6.circ as structural Verilog: 1 circuit, main circuit main
module main (
  output G,
  output Y,
  output R
);

  wire clock_1_out, j_k_ff_1_q, j_k_ff_1_qn, j_k_ff_2_q, or_1_out, or_2_out, or_3_out;

  Clock clock_1 (.out(clock_1_out));
  or or_1 (or_1_out, j_k_ff_2_q, j_k_ff_1_q);
  J_K_Flip_Flop j_k_ff_1 (
    .J(or_1_out), .clk(clock_1_out), .K(or_2_out), .Q(j_k_ff_1_q), .Qn(j_k_ff_1_qn));  // open: preset, en, reset
  or or_2 (or_2_out, j_k_ff_1_qn, j_k_ff_2_q);
  J_K_Flip_Flop j_k_ff_2 (
    .J(or_2_out), .clk(clock_1_out), .K(or_3_out), .Q(j_k_ff_2_q), .Qn(R));  // open: preset, en, reset
  or or_3 (or_3_out, R, j_k_ff_1_q);
  and and_1 (G, j_k_ff_1_qn, j_k_ff_2_q);
  and and_2 (Y, j_k_ff_1_q, j_k_ff_2_q);
endmodule
