// Logisim project hw8.circ as structural Verilog: 1 circuit, main circuit main
module main (
  input  [2:0] A15_A14_A13,
  input  D2,
  input  D1,
  input  D0
);

  wire d_ff_1_q, d_ff_2_q, d_ff_3_q, decoder_1_out4, E_out;

  Clock E (.out(E_out));
  Decoder #(.select(3)) decoder_1 (
    .out4(decoder_1_out4), .sel(A15_A14_A13), .en(E_out));  // open: out0, out1, out2, out3, out5, out6, out7
  D_Flip_Flop #(.trigger("high")) d_ff_1 (.clk(decoder_1_out4), .D(D2), .Q(d_ff_1_q));  // open: Qn, preset, en, reset
  LED Red (.in(d_ff_1_q));
  LED Yellow (.in(d_ff_2_q));
  D_Flip_Flop #(.trigger("high")) d_ff_2 (.clk(decoder_1_out4), .D(D1), .Q(d_ff_2_q));  // open: Qn, preset, en, reset
  LED Green (.in(d_ff_3_q));
  D_Flip_Flop #(.trigger("high")) d_ff_3 (.clk(decoder_1_out4), .D(D0), .Q(d_ff_3_q));  // open: Qn, preset, en, reset
endmodule
