// Logisim project hw8b.circ as structural Verilog: 1 circuit, main circuit main
module main (
  input  [2:0] A15_A14_A13,
  input  D0,
  output Device
);

  wire decoder_1_out4, E_out;

  Clock E (.out(E_out));
  Decoder #(.select(3)) decoder_1 (
    .out4(decoder_1_out4), .sel(A15_A14_A13), .en(E_out));  // open: out0, out1, out2, out3, out5, out6, out7
  D_Flip_Flop #(.trigger("high")) d_ff_1 (.clk(decoder_1_out4), .D(D0), .Q(Device));  // open: Qn, preset, en, reset
endmodule
