// Logisim project adder.circ as structural Verilog: 1 circuit, main circuit main
module main (
  input  SW1,
  input  SW2,
  input  SW1_2,
  input  SW1_3,
  input  SW2_2,
  input  SW2_3,
  input  SW3,
  input  SW3_2,
  output L4,
  output L3,
  output _11,
  output L4_2,
  output L3_2,
  output L3_3
);

  wire _04_2_out, _04_3_out, _04_4_out, _04_5_out, _04_6_out, _04_out, _08_2_out, _08_3_out, _08_4_out,
       _08_5_out, _08_6_out, _08_7_out, _08_8_out, _08_9_out, _08_10_out, _08_11_out, _32_5_out, _32_out,
       _86_2_out, _86_out;

  and _08 (L4, SW1, SW1, SW2);
  not _04 (_04_out, SW1);
  and _08_2 (_08_2_out, _04_out, SW2);
  and _08_3 (_08_3_out, SW1, _04_2_out);
  not _04_2 (_04_2_out, SW2);
  xor _86 (_86_out, SW2_2, SW3);
  not _04_3 (_04_3_out, SW1_2);
  or _32 (_32_out, SW2_2, SW3);
  not _04_4 (_04_4_out, _86_out);
  not _04_5 (_04_5_out, SW1_2);
  and _08_4 (_08_4_out, _04_3_out, SW2_2);
  or _32_2 (L3, _08_2_out, _08_3_out);
  and _08_5 (_08_5_out, _08_4_out, SW3);
  and _08_6 (_08_6_out, SW1_2, _04_4_out);
  and _08_7 (_08_7_out, _04_5_out, _86_out);
  and _08_8 (_08_8_out, SW1_2, _32_out);
  or _32_3 (_11, _08_6_out, _08_7_out);
  or _32_4 (L3_2, _08_5_out, _08_8_out);
  xor _86_2 (_86_2_out, SW2_3, SW3_2);
  not _04_6 (_04_6_out, SW1_3);
  or _32_5 (_32_5_out, SW2_3, SW3_2);
  and _08_9 (_08_9_out, _04_6_out, SW2_3);
  xor _86_3 (L4_2, SW1_3, _86_2_out);
  and _08_10 (_08_10_out, _08_9_out, SW3_2);
  and _08_11 (_08_11_out, SW1_3, _32_5_out);
  or _32_6 (L3_3, _08_10_out, _08_11_out);

  // Notes on the sheet:
  //   13
  //   12
  //   9
  //   10
  //   9
  //   13
  //   11
  //   11
  //   4
  //   8
  //   5
  //   8
  //   12
  //   10
  //   6
  //   13
  //   12
  //   10
  //   9
  //   1
  //   2
  //   13
  //   12
  //   11
  //   13
  //   12
  //   8
  //   3
  //   4
  //   5
  //   11
  //   L4
  //   6
  //   13
  //   12
  //   9
  //   10
  //   9
  //   11
  //   8
  //   4
  //   5
  //   8
  //   10
  //   9
  //   6
  //   2
  //   8
  //   1
  //   3
  //   13
  //   11
  //   12
  //   4
  //   5
  //   6
endmodule
