// Logisim project lab4.circ as structural Verilog: 1 circuit, main circuit main
module main (
  output Green,
  output Yellow,
  output Red
);

  wire _08_2_out, _08_3_out, _08_4_out, _08_5_out, _08_out, _32_2_out, _32_3_out, _32_out, _74___D0_q,
       _74___D0_qn, _74___D1_qn, _74___D2_q, _74___D2_qn, clock_1_out;

  Clock clock_1 (.out(clock_1_out));
  D_Flip_Flop _74___D2 (.clk(clock_1_out), .D(_08_out), .Q(_74___D2_q), .Qn(_74___D2_qn));  // open: preset, en, reset
  and _08 (_08_out, _08_2_out, Red);
  D_Flip_Flop _74___D1 (.clk(clock_1_out), .D(_08_4_out), .Q(Red), .Qn(_74___D1_qn));  // open: preset, en, reset
  D_Flip_Flop _74___D0 (
    .clk(clock_1_out), .D(_74___D1_qn), .Q(_74___D0_q), .Qn(_74___D0_qn));  // open: preset, en, reset
  and _08_2 (_08_2_out, _74___D0_qn, _74___D2_qn);
  or _32 (_32_out, Red, _74___D0_q);
  and _08_3 (_08_3_out, _74___D2_q, Red);
  and _08_4 (_08_4_out, _74___D2_qn, _32_out);
  or _32_2 (_32_2_out, _74___D2_q, Red);
  and _08_5 (_08_5_out, _74___D0_q, _74___D1_qn);
  or _32_3 (_32_3_out, _32_2_out, _74___D0_q);
  or _32_4 (Yellow, _08_3_out, _08_5_out);
  not _04 (Green, _32_3_out);

  // Notes on the sheet:
  //   11
  //   12
  //   5
  //   3
  //   6
  //   2
  //   13
  //   11
  //   12
  //   11
  //   9
  //   12
  //   8
  //   9
  //   8
  //   13
  //   11
  //   12
  //   13
  //   11
  //   12
  //   4
  //   5
  //   10
  //   9
  //   10
  //   8
  //   9
  //   6
  //   1
  //   2
  //   8
  //   1
  //   2
  //   3
  //   13
  //   3
  //   4
  //   6
  //   5
  //   12
endmodule
